# Fritzing sketch perfboard (saved by Fritzing 0.9.3b)
stripboards: 2

parts:
  Q2 = Basic FET N-Channel [package="D2Pak [SMD]"]  # not connected
  J1 = Camdenboss CTB0158-2 [part_number=CTB0158-2 package=THT]  # not connected
  U2 = atmega328 [package=dip]
  Y2 = Resonator [frequency="16 Mhz" package=THT]
  S3 = Momentary Switch [package=ksa_sealed_tac_switch]  # not connected
  R12 = Resistor [tolerance=±5% resistance=10k package=THT]
  R13 = Resistor [tolerance=±5% resistance=10k package=THT]
  R14 = Resistor [tolerance=±5% resistance=10k package=THT]
  R15 = Resistor [tolerance=±5% resistance=10k package=THT]
  JP2 = Header 3 [package=molex-1x3_lock]
  J3 = female pin header, 4 pins [form="♀ (female)"]
  J4 = female pin header, 5 pins [form="♀ (female)"]
  Q13 = TRANSISTOR_NPN [package=to-92]
  J5 = female pin header, 6 pins [form="♀ (female)"]
  J6 = female pin header, 3 pins [form="♀ (female)"]
  Q14 = TRANSISTOR_NPN [package=to-92]
  U3 = atmega328 [package=dip]
  Y3 = Resonator [frequency="16 Mhz" package=THT]
  S4 = Momentary Switch [package=ksa_sealed_tac_switch]  # not connected
  R16 = Resistor [tolerance=±5% resistance=10k package=THT]
  R17 = Resistor [tolerance=±5% resistance=10k package=THT]
  R18 = Resistor [tolerance=±5% resistance=10k package=THT]
  R19 = Resistor [tolerance=±5% resistance=10k package=THT]
  JP3 = Header 3 [package=molex-1x3_lock]
  J7 = female pin header, 4 pins [form="♀ (female)"]
  J8 = female pin header, 3 pins [form="♀ (female)"]
  J9 = female pin header, 6 pins [form="♀ (female)"]
  J10 = female pin header, 5 pins [form="♀ (female)"]
  R20 = Resistor [tolerance=±5% resistance=10k package=THT]  # not connected

nets:
  N1: U2.D0_(RX), J5.pin3
  N2: U2.XLAT1, U2.XLAT2, Y2.0, Y2.GND, Y2.pin_1
  N3: U2.D9_(PWM), R14.Pin_1
  N4: U2.D10_(PWM), R15.Pin_1
  N5: U2.AVCC, U2.AREF
  N6: U2.A3, J6.pin2
  N7: U2.A4, J3.pin3, J4.pin2
  N8: R12.Pin_0, R13.Pin_0, JP2.1, JP2.2
  N9: J3.pin1, Q13.C
  N10: J3.pin2, J4.pin1
  N11: J3.pin4, J4.pin3
  N12: J4.pin5, Q14.E
  N13: Q13.E, Q14.C
  N14: U3.D0_(RX), J9.pin4
  N15: U3.D1_(TX), J9.pin5
  N16: U3.XLAT1, U3.XLAT2, Y3.0, Y3.GND, Y3.pin_1
  N17: U3.D9_(PWM), R17.Pin_1
  N18: U3.D10_(PWM), R16.Pin_1
  N19: U3.AVCC, U3.AREF
  N20: U3.A3, J8.pin2
  N21: U3.A4, J7.pin3, J10.pin2
  N22: R18.Pin_0, R19.Pin_0, JP3.1, JP3.2
  N23: J7.pin2, J8.pin3, J10.pin1
  N24: J7.pin4, J10.pin3
